# Fritzing sketch Circuit (saved by Fritzing 0.9.3b)
circuit board: 8.46667cm x 5.64444cm
breadboards: 1

parts:
  ESP8266 = IC, DIP package, 20 pins [chip_label=IC]
  R1 = Resistor [tolerance=±5% resistance=220 package=THT]
  LED1 = LED - 5mm [color="Red (633nm)" package="5 mm [THT]"]
  S1 = Pushbutton [package="[THT]"]
  R2 = Resistor [tolerance=±5% resistance=220 package=THT]
  J1 = Basic Servo

nets:
  N1: ESP8266.pin1, S1.Pin_1, S1.Pin_2
  N2: ESP8266.pin7, J1.pulse
  N3: ESP8266.pin9, J1.gnd
  N4: ESP8266.pin11, J1.vcc
  N5: ESP8266.pin12, R1.Pin_0
  N6: ESP8266.pin13, LED1.anode
  N7: ESP8266.pin16, S1.Pin_4, R2.Pin_0
  N8: R1.Pin_1, LED1.cathode, R2.Pin_1
